# Fritzing sketch rgb-led-coaster-with-bluetooth (saved by Fritzing 0.9.0b)

parts:
  부품1 = Arduino Uno (Rev3)
  LED1 = RGB LED (com. cathode, rgb) [package="5 mm [THT]"]
  부품2 = Bluetooth Mate Silver

nets:
  N1: 부품1.D9_PWM, LED1.blue_anode
  N2: 부품1.D10_PWM/SS, LED1.green_anode
  N3: 부품1.D11_PWM/MOSI, LED1.common_cathode
  GND: 부품1.GND, LED1.red_anode, 부품2.GND
  N4: 부품1.D0/RX, 부품2.TX_5V
  N5: 부품1.D1/TX, 부품2.RX_5V
  5V: 부품1.5V, 부품2.VCC
